# Fritzing sketch ev-peripherals (saved by Fritzing 0.9.3b)
breadboards: 1

parts:
  Onderdeel1 = Arduino Mega 2560 (Rev3)
  DS1 = DS18B20 1-Wire Temperature Sensor [part_number=DS18B20]
  DS2 = DS18B20 1-Wire Temperature Sensor [part_number=DS18B20]
  DS3 = DS18B20 1-Wire Temperature Sensor [part_number=DS18B20]
  R1 = Resistor [tolerance=±5% resistance=220 package=THT]
  U3 = mystery part, 3 pins [chip_label=Flow]
  D1 = Zener Diode [part_number=1N4732A breakdown_voltage=3.6V package="Melf DO-213 AB [SMD]"]
  U4 = mystery part, 3 pins [chip_label=?]  # not connected
  U5 = mystery part, 3 pins [chip_label=?]
  LCD1 = LCD screen  # not connected
  Onderdeel2 = Adafruit I2C+SPI LCD Backpack [part_number="Adafruit #292"]
  U6 = mystery part, 3 pins [chip_label=Flow]
  U7 = mystery part, 3 pins [chip_label=Flow]

nets:
  N1: Onderdeel1.D21/SCL, Onderdeel2.LATCH
  N2: Onderdeel1.D20/SDA, Onderdeel2.DATA
  N3: Onderdeel1.D18/TX1, U7.pin3
  N4: Onderdeel1.D12_PWM, DS1.DQ, DS2.DQ, DS3.DQ, R1.Pin_1
  5V: Onderdeel1.5V, R1.Pin_0, U3.pin1, D1.anode, Onderdeel2.VCC, U6.pin1, U7.pin1
  GND: Onderdeel1.GND, U3.pin2, U5.pin3, Onderdeel2.GND, U6.pin2, U7.pin2
  N5: Onderdeel1.D2_PWM, U3.pin3
  N6: Onderdeel1.D3_PWM, U6.pin3
  N7: Onderdeel1.D6_PWM, U5.pin2
  VDD: DS1.VDD, DS2.VDD, DS3.VDD
  GND_2: DS1.GND, DS2.GND, DS3.GND
  N8: D1.cathode, U5.pin1

notes:
  12V 12V 12V
  GND PWM +

custom parts:
  LCD screen: A standard character display, usually with 2x16 characters. Comes in many colors.
  Adafruit I2C+SPI LCD Backpack: LCD backpacks reduce the number of pins needed to connect to an LCD. LCDs are a fun and easy way to have your microcontroller project talk back to you. Character LCDs are common, and easy to get, available in tons of colors and sizes. We've written tutorials on using character LCDs with an Arduino (or similar microcontroller) but find that the number of pins necessary to control the LCD can be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
